// Logisim project RegFile_ALU.circ as structural Verilog: 6 circuits, main circuit main
module main (
  input  [7:0] in_1,
  input  in_2,
  input  [2:0] in_3,
  input  [2:0] in_4,
  input  [7:0] in_5,
  input  [7:0] in_6,
  input  [2:0] in_7,
  output [7:0] out_8,
  output [7:0] out_9
);

  wire clock_1_out;

  Clock clock_1 (.out(clock_1_out));
  ALU alu_1 (.A(in_6), .B(in_5), .XYZ(in_7), .out_4(out_9));
  Reg_File reg_file_1 (.c(in_1), .load(in_2), .a_2_0(in_3), .in_5(in_4), .out_6(out_8), .in_2(clock_1_out));

  // Notes on the sheet:
  //   Oscar Valdés
  //   XYZ     Operation
  //   000      A + B
  //   001      A - B
  //   010      A + 1
  //   011      A
  //   100      A And B
  //   101      A Or B
  //   110      A Xor B
  //   111      Not A
endmodule

module ALU (
  input  [7:0] A,
  input  [7:0] B,
  input  [2:0] XYZ,
  output [7:0] out_4
);

  wire al_ext_1_out_4;
  wire [7:0] adder_1_out, al_ext_1_out_5, and_1_out, multiplexer_2_out, not_1_out, or_1_out, xor_1_out;

  AL_ext al_ext_1 (.in_2(XYZ[1]), .in_3(XYZ[0]), .out_5(al_ext_1_out_5), .in_1(B), .out_4(al_ext_1_out_4));
  Adder adder_1 (.a(al_ext_1_out_5), .b(A), .out(adder_1_out), .cin(al_ext_1_out_4));  // open: cout
  assign or_1_out = A | B;  // OR_Gate or_1, 8 bits wide
  assign and_1_out = A & B;  // AND_Gate and_1, 8 bits wide
  Multiplexer #(.width(8)) multiplexer_1 (
    .in0(adder_1_out), .in1(multiplexer_2_out), .out(out_4), .sel(XYZ[2]), .en(1'b1));
  assign not_1_out = ~A;  // NOT_Gate not_1, 8 bits wide
  assign xor_1_out = A ^ B;  // XOR_Gate xor_1, 8 bits wide
  Multiplexer #(.select(2), .width(8)) multiplexer_2 (
    .in0(and_1_out), .in1(or_1_out), .in2(xor_1_out), .in3(not_1_out), .out(multiplexer_2_out),
    .sel(XYZ[1:0]), .en(XYZ[2]));
endmodule

module Reg_File (
  input  [7:0] c,
  input  in_2,
  input  load,
  input  [2:0] a_2_0,
  input  [2:0] in_5,
  output [7:0] out_6
);

  wire decoder_1_out0, decoder_1_out1, decoder_1_out2, decoder_1_out3, decoder_1_out4, decoder_1_out5,
       decoder_1_out6, decoder_1_out7;
  wire [7:0] register_1_q, register_2_q, register_3_q, register_4_q, register_5_q, register_6_q,
       register_7_q, register_8_q;

  Decoder #(.select(3), .disabled(0)) decoder_1 (
    .out0(decoder_1_out0), .out1(decoder_1_out1), .out2(decoder_1_out2), .out3(decoder_1_out3),
    .out4(decoder_1_out4), .out5(decoder_1_out5), .out6(decoder_1_out6), .out7(decoder_1_out7), .sel(a_2_0),
    .en(load));
  Register register_1 (.D(c), .en(decoder_1_out0), .Q(register_1_q), .clk(in_2));  // open: clr
  Register register_2 (.D(c), .en(decoder_1_out1), .Q(register_2_q), .clk(in_2));  // open: clr
  Register register_3 (.D(c), .en(decoder_1_out2), .Q(register_3_q), .clk(in_2));  // open: clr
  Register register_4 (.D(c), .en(decoder_1_out3), .Q(register_4_q), .clk(in_2));  // open: clr
  Register register_5 (.D(c), .en(decoder_1_out4), .Q(register_5_q), .clk(in_2));  // open: clr
  Register register_6 (.D(c), .en(decoder_1_out5), .Q(register_6_q), .clk(in_2));  // open: clr
  Register register_7 (.D(c), .en(decoder_1_out6), .Q(register_7_q), .clk(in_2));  // open: clr
  Register register_8 (.D(c), .en(decoder_1_out7), .Q(register_8_q), .clk(in_2));  // open: clr
  Multiplexer #(.select(3), .width(8)) multiplexer_1 (
    .in0(register_1_q), .in1(register_2_q), .in2(register_3_q), .in3(register_4_q), .in4(register_5_q),
    .in5(register_6_q), .in6(register_7_q), .in7(register_8_q), .out(out_6), .sel(in_5), .en(1'b1));
endmodule

module AL_ext (
  input  [7:0] in_1,
  input  in_2,
  input  in_3,
  output out_4,
  output [7:0] out_5
);

  bext bext_1 (.in_2(in_2), .in_3(in_3), .out_4(out_5[7]), .in_1(in_1[7]));
  bext bext_2 (.in_2(in_2), .in_3(in_3), .out_4(out_5[6]), .in_1(in_1[6]));
  bext bext_3 (.in_2(in_2), .in_3(in_3), .out_4(out_5[3]), .in_1(in_1[3]));
  bext bext_4 (.in_2(in_2), .in_3(in_3), .out_4(out_5[4]), .in_1(in_1[4]));
  bext bext_5 (.in_2(in_2), .in_3(in_3), .out_4(out_5[5]), .in_1(in_1[5]));
  bext bext_6 (.in_2(in_2), .in_3(in_3), .out_4(out_5[0]), .in_1(in_1[0]));
  cext cext_1 (.in_1(in_2), .in_2(in_3), .out_3(out_4));
  bext bext_7 (.in_2(in_2), .in_3(in_3), .out_4(out_5[1]), .in_1(in_1[1]));
  bext bext_8 (.in_2(in_2), .in_3(in_3), .out_4(out_5[2]), .in_1(in_1[2]));
endmodule

module bext (
  input  in_1,
  input  in_2,
  input  in_3,
  output out_4
);

  wire not_1_out, xor_1_out;

  not not_1 (not_1_out, in_2);
  and and_1 (out_4, not_1_out, xor_1_out);
  xor xor_1 (xor_1_out, in_1, in_3);
endmodule

module cext (
  input  in_1,
  input  in_2,
  output out_3
);

  xor xor_1 (out_3, in_1, in_2);
endmodule
